# Fritzing sketch file 11 (saved by Fritzing 0.9.4)
breadboards: 1

parts:
  LED1 = LED - 5mm [color="Red (633nm)" package="5 mm [THT]"]
  LED2 = LED - 5mm [color="Red (633nm)" package="5 mm [THT]"]
  LED3 = LED - 5mm [color="Red (633nm)" package="5 mm [THT]"]
  LED4 = LED - 5mm [color="Red (633nm)" package="5 mm [THT]"]
  LED5 = LED - 5mm [color="Red (633nm)" package="5 mm [THT]"]
  LED6 = LED - 5mm [color="Red (633nm)" package="5 mm [THT]"]
  S1 = Pushbutton [package="[THT]"]
  Part1 = Arduino Uno (Rev3)

nets:
  N1: LED1.cathode, LED2.cathode, LED3.cathode, LED4.cathode, LED5.cathode, LED6.cathode, S1.Pin_3, S1.Pin_4, Part1.GND
  N2: LED1.anode, Part1.D7
  N3: LED2.anode, Part1.D6_PWM
  N4: LED3.anode, Part1.D5_PWM
  N5: LED4.anode, Part1.D4
  N6: LED5.anode, Part1.D3_PWM
  N7: LED6.anode, Part1.D2
  N8: S1.Pin_1, S1.Pin_2, Part1.RESET
