# Fritzing sketch file 13 (saved by Fritzing 0.9.4)
breadboards: 1

parts:
  LED3 = LED - 5mm [color="Red (633nm)" package="5 mm [THT]"]
  Part1 = Arduino Uno (Rev3)
  R1 = Rotary Potentiometer (Small) [maximum_resistance=100kΩ package=THT]
  R2 = Resistor [tolerance=±5% resistance=220 package=THT]

nets:
  N1: LED3.cathode, R2.Pin_0
  N2: LED3.anode, Part1.D9_PWM
  N3: Part1.A0, R1.wiper
  N4: Part1.5V, R1.leg1
  N5: Part1.GND, R1.leg2, R2.Pin_1
