# Fritzing sketch file 16 (saved by Fritzing 0.9.4)
breadboards: 1

parts:
  LED1 = LED - 5mm [color="Red (633nm)" package="5 mm [THT]"]
  LED2 = LED - 5mm [color="Red (633nm)" package="5 mm [THT]"]
  LED3 = LED - 5mm [color="Red (633nm)" package="5 mm [THT]"]
  Part1 = Arduino Uno (Rev3)

nets:
  N1: LED1.cathode, LED2.cathode, LED3.cathode, Part1.GND
  N2: LED1.anode, LED2.anode, LED3.anode, Part1.D9_PWM
